// Logisim project encoder (1).circ as structural Verilog: 1 circuit, main circuit main
// 8
module main (
  output out_1,
  output out_2,
  output out_3,
  output out_4,
  output out_5
);

  wire multiplexer_1_out, multiplexer_2_out, multiplexer_3_out, multiplexer_4_out, multiplexer_5_out,
       multiplexer_6_out, multiplexer_7_out, multiplexer_8_out, or_4_out, undriven;

  Multiplexer multiplexer_1 (.in0(1'b1), .in1(1'b0), .out(multiplexer_1_out), .sel(1'b0));  // open: en
  Multiplexer multiplexer_2 (.in0(1'b0), .in1(1'b0), .out(multiplexer_2_out), .sel(1'b0));  // open: en
  Multiplexer multiplexer_3 (.in0(1'b0), .in1(1'b0), .out(multiplexer_3_out), .sel(1'b0));  // open: en
  Multiplexer multiplexer_4 (.in0(1'b0), .in1(1'b0), .out(multiplexer_4_out), .sel(1'b0));  // open: en
  Multiplexer multiplexer_5 (
    .in0(multiplexer_1_out), .in1(multiplexer_2_out), .out(multiplexer_5_out), .sel(1'b0));  // open: en
  Multiplexer multiplexer_6 (
    .in0(multiplexer_3_out), .in1(multiplexer_4_out), .out(multiplexer_6_out), .sel(1'b0));  // open: en
  Multiplexer #(.select(3)) multiplexer_7 (
    .in0(1'b0), .in1(1'b0), .in2(1'b0), .in3(1'b0), .in4(1'b0), .in5(1'b0), .in6(1'b0), .in7(1'b1),
    .out(multiplexer_7_out), .sel(3'b111), .en(1'b1));
  LED led_1 (.in(multiplexer_7_out));
  Multiplexer multiplexer_8 (
    .in0(multiplexer_5_out), .in1(multiplexer_6_out), .out(multiplexer_8_out), .sel(1'b0));  // open: en
  LED led_2 (.in(multiplexer_8_out));
  or or_1 (out_4, 1'b0, 1'b1);
  or or_2 (out_5, 1'b0, 1'b0);
  // OR_Gate or_3 has open pins: in0=undriven, out=open
  buf or_4 (or_4_out, undriven);  // OR_Gate
  // OR_Gate or_5 has open pins: in0=undriven, out=open
  // OR_Gate or_6 has open pins: in0=undriven, out=open
  Priority_Encoder priority_encoder_1 (
    .in0(1'b0), .in1(1'b0), .in2(1'b0), .in3(1'b0), .in4(1'b0), .in5(1'b0), .in6(1'b0), .in7(1'b1),
    .out({out_3, out_2, out_1}));  // open: en_in, gs, en_out
endmodule
