// Logisim project FULL_ADDER.circ as structural Verilog: 1 circuit, main circuit main
module main (
);

  wire and_1_out, and_2_out, nand_1_out, nand_2_out, nand_3_out, nand_4_out, nand_5_out, nand_6_out,
       nand_7_out, nand_8_out, nand_9_out, or_1_out, xor_1_out, xor_2_out;

  nand nand_1 (nand_1_out, 1'b0, 1'b0);
  xor xor_1 (xor_1_out, 1'b0, 1'b0);
  and and_1 (and_1_out, 1'b0, 1'b0);
  nand nand_2 (nand_2_out, 1'b0, nand_1_out);
  nand nand_3 (nand_3_out, nand_1_out, 1'b0);
  nand nand_4 (nand_4_out, nand_2_out, nand_3_out);
  and and_2 (and_2_out, xor_1_out, 1'b1);
  xor xor_2 (xor_2_out, xor_1_out, 1'b1);
  nand nand_5 (nand_5_out, nand_4_out, 1'b1);
  or or_1 (or_1_out, and_2_out, and_1_out);
  nand nand_6 (nand_6_out, nand_4_out, nand_5_out);
  nand nand_7 (nand_7_out, nand_5_out, 1'b1);
  LED led_1 (.in(xor_2_out));
  LED led_2 (.in(or_1_out));
  LED led_3 (.in(nand_8_out));
  nand nand_8 (nand_8_out, nand_6_out, nand_7_out);
  nand nand_9 (nand_9_out, nand_1_out, nand_5_out);
  LED led_4 (.in(nand_9_out));
endmodule
